// Logisim project processador MIPS.circ as structural Verilog: 5 circuits, main circuit main
module main (
  input  in_1
);

  wire ALUSrc, and_1_out, Branch, CLK, EQUAL, Jump, MemRead, MemToReg, MemWrite, not_1_out, or_1_out, RegDst,
       RegWrite;
  wire [1:0] ALUOp;
  wire [2:0] controlador_da_ula_1_ulactrl, multiplexer_1_out, Opcode, rs, rt;
  wire [2:2] rd;
  wire [7:0] adder_1_out, Banco_de_Registradores_readdata1, DataRt, Endereco, multiplexer_2_out,
       multiplexer_3_out, ram_1_data, register_1_q, ResULA, WriteData;

  Clock clock_1 (.out(CLK));
  Register register_1 (.D(multiplexer_2_out), .Q(register_1_q), .clk(CLK), .clr(in_1));  // open: en
  Adder adder_1 (.a(8'h1), .b(register_1_q), .out(adder_1_out));  // open: cin, cout
  Multiplexer #(.width(3), .enable("false")) multiplexer_1 (
    .in0(rt), .in1({rd[2], Endereco[7:6]}), .out(multiplexer_1_out), .sel(RegDst));
  and and_1 (and_1_out, EQUAL, Branch);
  or or_1 (or_1_out, Jump, and_1_out);
  ROM #(.dataWidth(18)) rom_1 (.addr(register_1_q), .data({Opcode, rs, rt, rd[2], Endereco}));  // open: sel
  Banco_de_Registradores Banco_de_Registradores (
    .ReadReg1(rs), .ReadReg2(rt), .WriteData(WriteData), .WriteReg(multiplexer_1_out), .CLEAR(in_1),
    .CLOCK(CLK), .ReadWrite(RegWrite), .ReadData1(Banco_de_Registradores_readdata1), .ReadData2(DataRt));
  Controlador_da_ULA controlador_da_ula_1 (
    .FUNCT(Endereco[2:0]), .ALUOp(ALUOp), .ULACtrl(controlador_da_ula_1_ulactrl));
  Multiplexer #(.width(8), .enable("false")) multiplexer_2 (
    .in0(adder_1_out), .in1(Endereco), .out(multiplexer_2_out), .sel(or_1_out));
  Multiplexer #(.width(8), .enable("false")) multiplexer_3 (
    .in0(DataRt), .in1(Endereco), .out(multiplexer_3_out), .sel(ALUSrc));
  ULA ULA (
    .A(Banco_de_Registradores_readdata1), .B(multiplexer_3_out), .\Função (controlador_da_ula_1_ulactrl),
    .Deslocamento(Endereco[5:3]), .C(ResULA), .IGUAL(EQUAL));
  Unidade_de_Controle Unidade_de_Controle (
    .RegDst(RegDst), .RegWrite(RegWrite), .ALUSrc(ALUSrc), .MemWrite(MemWrite), .MemRead(MemRead),
    .MemToReg(MemToReg), .Branch(Branch), .Jump(Jump), .ALUOp(ALUOp), .Opcode(Opcode));
  not not_1 (not_1_out, CLK);
  RAM #(.bus("separate")) ram_1 (
    .addr(ResULA), .din(DataRt), .data(ram_1_data), .str(MemWrite), .clk(not_1_out), .ld(MemRead), .clr(in_1));  // open: sel
  Multiplexer #(.width(8), .enable("false")) multiplexer_4 (
    .in0(ResULA), .in1(ram_1_data), .out(WriteData), .sel(MemToReg));

  // Other names for the same wires on the sheet: funct[2:0] = Endereco[2:0]; rd[1:0] = Endereco[7:6]; RESET = in_1;
  //   shamt[2:0] = Endereco[5:3]

  // Notes on the sheet:
  //   contents of rom_1 (hex, n*v repeats v):
  //   19004 2282 1641 38000 10400
endmodule

module Banco_de_Registradores (
  input  [2:0] ReadReg1,
  input  [2:0] ReadReg2,
  input  [7:0] WriteData,
  input  [2:0] WriteReg,
  input  CLEAR,
  input  CLOCK,
  input  ReadWrite,
  output [7:0] ReadData1,
  output [7:0] ReadData2
);

  wire ER0, ER1, ER2, ER3, ER4, ER5, ER6, ER7;
  wire [7:0] R0, r0_t, R1, r1_t, R2, r2_t, R3, r3_t, R4, r4_t, R5, r5_t, R6, r6_t, R7, r7_t;

  Demultiplexer #(.select(3), .width(8), .enable("false")) demultiplexer_1 (
    .out0(r0_t), .out1(r1_t), .out2(r2_t), .out3(r3_t), .out4(r4_t), .out5(r5_t), .out6(r6_t), .out7(r7_t),
    .in(WriteData), .sel(WriteReg));
  Demultiplexer #(.select(3), .enable("false")) demultiplexer_2 (
    .out0(ER0), .out1(ER1), .out2(ER2), .out3(ER3), .out4(ER4), .out5(ER5), .out6(ER6), .out7(ER7),
    .in(ReadWrite), .sel(WriteReg));
  Register u_R0 (.D(r0_t), .en(ER0), .Q(R0), .clk(CLOCK), .clr(CLEAR));
  Register u_R1 (.D(r1_t), .en(ER1), .Q(R1), .clk(CLOCK), .clr(CLEAR));
  Register u_R2 (.D(r2_t), .en(ER2), .Q(R2), .clk(CLOCK), .clr(CLEAR));
  Register u_R3 (.D(r3_t), .en(ER3), .Q(R3), .clk(CLOCK), .clr(CLEAR));
  Register u_R4 (.D(r4_t), .en(ER4), .Q(R4), .clk(CLOCK), .clr(CLEAR));
  Register u_R5 (.D(r5_t), .en(ER5), .Q(R5), .clk(CLOCK), .clr(CLEAR));
  Register u_R6 (.D(r6_t), .en(ER6), .Q(R6), .clk(CLOCK), .clr(CLEAR));
  Register u_R7 (.D(r7_t), .en(ER7), .Q(R7), .clk(CLOCK), .clr(CLEAR));
  Multiplexer #(.select(3), .width(8), .enable("false")) multiplexer_1 (
    .in0(R0), .in1(R1), .in2(R2), .in3(R3), .in4(R4), .in5(R5), .in6(R6), .in7(R7), .out(ReadData1),
    .sel(ReadReg1));
  Multiplexer #(.select(3), .width(8), .enable("false")) multiplexer_2 (
    .in0(R0), .in1(R1), .in2(R2), .in3(R3), .in4(R4), .in5(R5), .in6(R6), .in7(R7), .out(ReadData2),
    .sel(ReadReg2));

  // Other names for the same wires on the sheet: CLK = CLOCK; CLR = CLEAR
endmodule

module ULA (
  input  [7:0] A,
  input  [7:0] B,
  input  [2:0] \Função ,
  input  [2:0] Deslocamento,
  output [7:0] C,
  output IGUAL
);

  wire comparator_1_lt;
  wire [7:0] AComp, ADesCDir, ADesEsq, ADiv, AMult, ANeg, ASoma, ASub, BComp, BDesCDir, BDesEsq, BDiv, BMult,
       BNeg, BSoma, BSub, ResComp, ResDesDir, ResDesEsq, ResDiv, ResMult, ResNeg, ResSoma, ResSub;

  Demultiplexer #(.select(3), .width(8), .enable("false")) demultiplexer_1 (
    .out0(ASoma), .out1(ASub), .out2(AMult), .out3(ADiv), .out4(ANeg), .out5(AComp), .out6(ADesEsq),
    .out7(ADesCDir), .in(A), .sel(\Função ));
  Demultiplexer #(.select(3), .width(8), .enable("false")) demultiplexer_2 (
    .out0(BSoma), .out1(BSub), .out2(BMult), .out3(BDiv), .out4(BNeg), .out5(BComp), .out6(BDesEsq),
    .out7(BDesCDir), .in(B), .sel(\Função ));
  Adder adder_1 (.a(ASoma), .b(BSoma), .out(ResSoma));  // open: cin, cout
  Subtractor subtractor_1 (.a(ASub), .b(BSub), .out(ResSub));  // open: bin, bout
  Multiplier multiplier_1 (.a(AMult), .b(BMult), .out(ResMult));  // open: cin, cout
  Divider divider_1 (.a(ADiv), .b(BDiv), .out(ResDiv));  // open: upper, rem
  Negator negator_1 (.in(ANeg), .out(ResNeg));
  Comparator comparator_1 (.a(AComp), .b(BComp), .eq(IGUAL), .lt(comparator_1_lt));  // open: gt
  assign ResComp = {{7{1'b0}}, comparator_1_lt};  // Bit_Extender bit_extender_1
  Shifter shifter_1 (.in(ADesEsq), .\dist (Deslocamento), .out(ResDesEsq));
  Shifter #(.shift("lr")) shifter_2 (.in(ADesCDir), .\dist (Deslocamento), .out(ResDesDir));
  Multiplexer #(.select(3), .width(8), .enable("false")) multiplexer_1 (
    .in0(ResSoma), .in1(ResSub), .in2(ResMult), .in3(ResDiv), .in4(ResNeg), .in5(ResComp), .in6(ResDesEsq),
    .in7(ResDesDir), .out(C), .sel(\Função ));

  // Other names for the same wires on the sheet: DES[2:0] = Deslocamento; FUNCT[2:0] = \Função 
endmodule

module Unidade_de_Controle (
  input  [2:0] Opcode,
  output RegDst,
  output RegWrite,
  output ALUSrc,
  output MemWrite,
  output MemRead,
  output MemToReg,
  output Branch,
  output Jump,
  output [1:0] ALUOp
);

  wire and_1_out, and_4_out, and_5_out, and_8_out, and_9_out, nor_2_out, or_2_out;

  nor nor_1 (RegDst, Opcode[0], Opcode[1], Opcode[2]);
  nor nor_2 (nor_2_out, Opcode[1], Opcode[2]);
  and and_1 (and_1_out, ~Opcode[0], ~Opcode[1], Opcode[2]);  // AND_Gate
  ExactlyOne xor_1 (.out(ALUSrc), .in0(Opcode[0]), .in1(Opcode[1]), .in2(Opcode[2]));
  and and_2 (MemWrite, ~Opcode[0], Opcode[1], ~Opcode[2]);  // AND_Gate
  and and_3 (MemRead, Opcode[0], ~Opcode[1], ~Opcode[2]);  // AND_Gate
  and and_4 (and_4_out, ~Opcode[0], ~Opcode[1], ~Opcode[2]);  // AND_Gate
  and and_5 (and_5_out, ~Opcode[0], ~Opcode[1], Opcode[2]);  // AND_Gate
  and and_6 (Branch, Opcode[0], Opcode[1], ~Opcode[2]);  // AND_Gate
  and and_7 (Jump, Opcode[0], Opcode[1], Opcode[2]);
  and and_8 (and_8_out, Opcode[0], Opcode[1], ~Opcode[2]);  // AND_Gate
  and and_9 (and_9_out, ~Opcode[0], ~Opcode[1], Opcode[2]);  // AND_Gate
  and and_10 (ALUOp[1], ~Opcode[0], ~Opcode[1]);  // AND_Gate
  or or_1 (RegWrite, nor_2_out, and_1_out);
  or or_2 (or_2_out, and_4_out, and_5_out);
  not not_1 (MemToReg, or_2_out);
  or or_3 (ALUOp[0], and_8_out, and_9_out);
endmodule

module Controlador_da_ULA (
  input  [2:0] FUNCT,
  input  [1:0] ALUOp,
  output [2:0] ULACtrl
);

  Multiplexer #(.select(2), .width(3), .enable("false")) multiplexer_1 (
    .in0(3'b000), .in1(3'b101), .in2(FUNCT), .in3(3'b000), .out(ULACtrl), .sel(ALUOp));
endmodule
